# Fritzing sketch Vibration_motor_Automatic_BT_TOTAL (saved by Fritzing 0.8.7b)
breadboards: 2

parts:
  Componente1 = Arduino Uno (Rev3)
  U1 = OV7670 Camera [package=camera_sfv24r-2st_2]
  SW-1 = Vibration sensor module
  Componente2 = Bluetooth HC-05 Macho
  S1 = Pushbutton [package="[THT]"]
  Componente3 = SRF05 Ultrasonic Rangefinder
  R1 = Resistor [package="2512 [SMD]"]
  R2 = Resistor [tolerance=±5% resistance=220 package=THT]
  R3 = Resistor [tolerance=±5% resistance=220 package=THT]
  R4 = Resistor [tolerance=±5% resistance=220 package=THT]
  R5 = Resistor [tolerance=±5% resistance=220 package=THT]

nets:
  N1: Componente1.A0, U1.D0
  N2: Componente1.A1, U1.D1
  N3: Componente1.A2, U1.D2
  N4: Componente1.A3, U1.D3
  N5: Componente1.A4/SDA, U1.SIDO, R4.Pin_1
  N6: Componente1.A5/SCL, U1.SIOC, R3.Pin_1
  N7: Componente1.D8, SW-1.Digital_output
  N8: Componente1.D9_PWM, Componente3.Echo
  N9: Componente1.D10_PWM/SS, Componente3.Trig
  N10: Componente1.D11_PWM/MOSI, R5.Pin_0
  N11: Componente1.D12/MISO, U1.D7
  N12: Componente1.D13/SCK, U1.HREF
  GND: Componente1.GND, Componente1.D7, U1.GND, U1.PWDN, SW-1.Ground, Componente2.GND, S1.Pin_1, S1.Pin_2, Componente3.GND, R2.Pin_0
  N13: Componente1.D0/RX, Componente2.TXD
  N14: Componente1.D1/TX, Componente2.RXD
  N15: Componente1.D2, U1.PCLK
  N16: Componente1.D3_PWM, U1.VSYNC
  N17: Componente1.D4, U1.D4
  N18: Componente1.D5_PWM, U1.D5
  N19: Componente1.D6_PWM, U1.D6
  3V3: Componente1.3V3, U1.3V3, U1.RESET, R3.Pin_0, R4.Pin_0
  VCC: Componente1.5V, SW-1.vcc, Componente2.VCC, S1.Pin_3, S1.Pin_4, Componente3.VCC, R1.Pin_0
  N20: U1.XCLK, R2.Pin_1, R5.Pin_1

custom parts:
  OV7670 Camera: CMOS image sensor
  Vibration sensor module: Single-roller type full induction trigger switch. When no vibration or tilt, the product is ON conduction state, and in the steady state, when a vibration or tilt, the switch will be rendered instantly disconnect the conductive resistance increases, generating a current pulse signal, thereby triggering circuit. The default state of the swith is close Digital output Supply voltage:3.3V-5V On-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
