# Fritzing sketch Vibration_motor_Manual_BT (saved by Fritzing 0.8.7b)
breadboards: 1

parts:
  Componente1 = Arduino Uno (Rev3)
  SW-1 = Vibration sensor module
  Componente2 = Bluetooth HC-05 Macho
  Componente3 = SRF05 Ultrasonic Rangefinder
  D2F1 = D2F-FL Omron Snap Action Limit Switch with Level
  BAT1 = BC9VPC [package=bc9vpc]

nets:
  N1: Componente1.D8, SW-1.Digital_output
  N2: Componente1.D9_PWM, Componente3.Echo
  N3: Componente1.D10_PWM/SS, Componente3.Trig
  GND: Componente1.GND, SW-1.Ground, Componente2.GND, Componente3.GND, BAT1.V+
  N4: Componente1.D0/RX, Componente2.TXD
  N5: Componente1.D1/TX, Componente2.RXD
  VCC: Componente1.5V, SW-1.vcc, Componente2.VCC, Componente3.VCC
  N6: Componente1.VIN, D2F1.NC
  N7: D2F1.NO, BAT1.V-

custom parts:
  Vibration sensor module: Single-roller type full induction trigger switch. When no vibration or tilt, the product is ON conduction state, and in the steady state, when a vibration or tilt, the switch will be rendered instantly disconnect the conductive resistance increases, generating a current pulse signal, thereby triggering circuit. The default state of the swith is close Digital output Supply voltage:3.3V-5V On-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
  D2F-FL Omron Snap Action Limit Switch with Level: Snap action switch with stainless steel lever.
